# Fritzing sketch Nano photomicrosensor (saved by Fritzing 0.9.3b)
breadboards: 1
stripboards: 1

parts:
  Part1 = Arduino Nano (Rev3.0)
  R1 = Resistor [tolerance=±5% resistance=10k package="0402 [SMD]"]
  R2 = Resistor [tolerance=±5% resistance=1k package="0402 [SMD]"]

nets:
  N1: Part1.GND, R1.Pin_0, R2.Pin_0
  N2: Part1.A0, R2.Pin_1

notes:
  SX1137
  From top to bottom: Connectors 1 to 3
  Connections
  1 - Collector
  2 - E K
  3 - A
